# Fritzing sketch Arduino_Crepuscolare (saved by Fritzing 0.9.0b)
breadboards: 1

parts:
  LED1 = LED - 5mm [color="Red (633nm)" package="5 mm [THT]"]
  R1 = Resistor [tolerance=±5% resistance=100 package=THT]
  Componente1 = Arduino Uno (Rev3)
  R2 = PHOTOCELL [package=photocell-kit]
  R3 = Rotary Potentiometer (Large) [maximum_resistance=100kΩ package=THT]

nets:
  N1: LED1.anode, Componente1.D13/SCK
  N2: R1.Pin_0, Componente1.GND, R3.leg2
  N3: Componente1.A0, R2.P$1, R3.wiper
  N4: Componente1.5V, R2.P$2
